// Logisim project z80.circ as structural Verilog: 3 circuits, main circuit test
module test (
  input  [7:0] in_1,
  input  [7:0] in_2,
  input  in_3,
  input  in_4,
  input  in_5,
  input  in_6,
  input  [7:0] in_7,
  input  [7:0] in_8
);

  wire button_1_out, button_2_out;
  wire [7:0] register_2_q;
  wire [31:0] rom_1_data;

  Button button_1 (.out(button_1_out));
  Register register_1 (
    .D({in_4, in_3, in_6, {2{in_5}}, in_6, in_4, in_3}), .en(button_1_out), .clk(button_1_out));  // open: Q, clr
  ROM #(.dataWidth(32)) rom_1 (.addr(in_8), .data(rom_1_data));
  Button button_2 (.out(button_2_out));
  Register register_2 (.D(in_1), .en(button_2_out), .clk(button_2_out), .Q(register_2_q));  // open: clr
  // Probe on rom_1_data
  // Probe on register_2_q

  // Notes on the sheet:
  //   contents of rom_1 (hex, n*v repeats v):
  //   0 1 4*0 3 6*0 445 4*0 32214 0 0 0 41242145 22*0 5
endmodule

module databus8 (
  input  [7:0] in_1
);
endmodule

module IDynamicMemories_F23 (
  input  neg_RFSH,
  input  neg_MREQ,
  input  A12,
  input  [11:0] A11_A0,
  input  [7:0] in_5,
  input  neg_WR
);

  wire and_1_out, and_2_out, and_3_out, clk, or_1_out, or_2_out, Read, Write;
  wire [7:0] controlled_buffer_2_out, controlled_buffer_3_out;

  Clock clock_1 (.out(clk));
  Button button_1 ();  // open: out
  Controlled_Buffer controlled_buffer_1 ();  // open: in, out, en
  assign controlled_buffer_2_out = Write ? in_5 : 8'bz;  // Controlled_Buffer controlled_buffer_2
  assign controlled_buffer_3_out = Read ? controlled_buffer_2_out : 8'bz;  // Controlled_Buffer controlled_buffer_3
  // Probe on controlled_buffer_3_out
  D_Flip_Flop d_ff_1 (.D(neg_WR), .clk(clk), .Q(Write), .Qn(Read));  // open: preset, reset
  buf buffer_1 (neg_MREQ, A12);
  Button button_2 ();  // open: out
  and and_1 (and_1_out, ~neg_RFSH, ~neg_MREQ);  // AND_Gate
  and and_2 (and_2_out, ~neg_MREQ, ~A12);  // AND_Gate
  and and_3 (and_3_out, ~neg_MREQ, ~neg_MREQ);  // AND_Gate
  or or_1 (or_1_out, and_1_out, and_2_out);
  or or_2 (or_2_out, and_1_out, and_3_out);
  RAM #(.addrWidth(12), .clearpin("true"), .databus("bidir")) ram_1 (
    .addr(A11_A0), .we(Write), .oe(Read), .clk(clk), .data(controlled_buffer_2_out), .clr(or_2_out));
  RAM #(.addrWidth(12), .clearpin("true"), .databus("bidir")) ram_2 (
    .addr(A11_A0), .we(Write), .oe(Read), .clk(clk), .data(controlled_buffer_2_out), .clr(or_1_out));
endmodule
